# Fritzing sketch Analog Read (saved by Fritzing 0.8.3b)
breadboards: 1

parts:
  Resistor = Resistor [tolerance=±5% resistance=10k package=THT]
  Potentiometer = Trimmer Potentiometer [maximum_resistance=10kΩ package=THT]
  VCC = 4 x AAA Battery Mount

nets:
  AI: Resistor.Pin_0, Potentiometer.leg1
  N1: Resistor.Pin_1, VCC.-
  N2: Potentiometer.leg2, VCC.+
