# Fritzing sketch Photocell Circuit Schematic (saved by Fritzing 0.8.3b)
breadboards: 1

parts:
  Resistor = Resistor [tolerance=±5% resistance=10k package=THT]
  Vcc = 4 x AAA Battery Mount
  Photocell = Photocell (LDR) [package=THT]

nets:
  N1: Resistor.Pin_0, Vcc.-
  AI: Resistor.Pin_1, Photocell.pin_1
  N2: Vcc.+, Photocell.pin_0
